// Logisim project McComputer2Risc.circ as structural Verilog: 1 circuit, main circuit main
module main (
);

  wire adder_2_cout, and_1_out, and_2_out, and_3_out, and_4_out, and_5_out, and_6_out, and_8_out, and_9_out,
       and_10_out, and_12_out, and_16_out, and_23_out, and_25_out, and_27_out, and_28_out, ClearDsp_out,
       clock_1_out, comparator_1_eq, comparator_1_gt, comparator_1_lt, Condition_q, demultiplexer_1_out0,
       demultiplexer_1_out1, demultiplexer_1_out2, demultiplexer_1_out3, demultiplexer_1_out4,
       demultiplexer_1_out5, demultiplexer_2_out0, demultiplexer_2_out1, demultiplexer_2_out2,
       demultiplexer_2_out3, demultiplexer_2_out4, demultiplexer_2_out5, demultiplexer_2_out6,
       demultiplexer_2_out7, demultiplexer_3_out0, demultiplexer_3_out1, demultiplexer_3_out2,
       demultiplexer_3_out3, demultiplexer_3_out4, demultiplexer_3_out5, demultiplexer_3_out6,
       demultiplexer_3_out7, demultiplexer_3_out8, demultiplexer_3_out9, not_1_out, not_2_out, not_3_out,
       not_4_out, not_5_out, not_6_out, not_7_out, not_8_out, not_9_out, not_10_out, not_11_out, not_12_out,
       not_13_out, or_4_out, or_6_out, or_7_out, or_9_out, or_15_out, or_16_out, or_17_out, or_18_out,
       or_19_out, or_20_out, or_22_out, or_23_out, or_24_out, or_25_out, or_26_out, or_27_out, or_28_out,
       or_30_out, or_33_out, or_36_out, or_38_out, or_41_out, or_42_out, or_43_out, or_44_out, Overflow_q,
       register_1_q, Reset_out, rgb_video_1_p1;
  wire [0:0] InFlag_q;
  wire [1:0] Color_q;
  wire [2:0] X_q, Y_q;
  wire [3:0] register_2_q;
  wire [4:0] rgb_video_1_p4, rgb_video_1_p5;
  wire [7:0] adder_1_out, adder_2_out, AluIeft_q, AluOut_q, AluRight_q, and_7_out, and_11_out, and_13_out,
       and_14_out, and_15_out, and_17_out, and_18_out, and_19_out, and_20_out, and_21_out, and_22_out,
       and_24_out, and_26_out, and_29_out, and_30_out, and_31_out, bit_extender_2_out, bit_extender_3_out,
       bit_extender_4_out, bit_extender_5_out, bit_extender_6_out, bit_extender_7_out, bit_extender_8_out,
       bit_extender_9_out, bit_extender_10_out, bit_extender_11_out, bit_extender_12_out,
       bit_extender_13_out, bit_extender_14_out, bit_extender_15_out, bit_extender_16_out, DataIn_q,
       Disc_dout, multiplexer_1_out, multiplexer_3_out, multiplexer_4_out, multiplexer_5_out,
       multiplexer_6_out, multiplexer_7_out, multiplexer_8_out, multiplexer_9_out, multiplexer_10_out,
       multiplexer_11_out, multiplexer_12_out, multiplexer_13_out, multiplexer_14_out, multiplexer_15_out,
       multiplexer_16_out, multiplexer_17_out, multiplexer_18_out, multiplexer_19_out, multiplexer_20_out,
       multiplexer_21_out, multiplexer_22_out, multiplexer_23_out, multiplexer_24_out, multiplexer_25_out,
       or_1_out, or_3_out, or_5_out, or_8_out, or_10_out, or_11_out, or_13_out, or_14_out, or_21_out,
       or_31_out, or_32_out, or_34_out, or_35_out, or_37_out, or_39_out, or_40_out, Page_q, PgCounter_q,
       PgCounter_q_2, PtrReg_q, Ram256_dout, register_3_q, register_4_q, register_5_q, register_6_q,
       register_7_q, register_8_q, register_9_q, register_10_q, register_11_q, register_12_q, register_13_q,
       register_14_q, register_15_q, register_16_q, register_17_q, register_18_q, register_19_q,
       register_20_q, register_21_q, register_22_q, register_23_q, register_24_q, register_25_q,
       Registers_dout, shifter_1_out, shifter_2_out, subtractor_1_out, xor_1_out, xor_2_out, xor_3_out,
       xor_4_out, xor_5_out, xor_6_out, xor_7_out, xor_8_out, xor_9_out;
  wire [14:0] rgb_video_1_p6;
  wire [15:0] multiplexer_2_out;
  wire [23:0] rom_1_data;
  wire [27:0] register_2_q_2;
  wire [31:0] bit_extender_1_out, or_2_out, rom_2_data;
  wire [31:24] rom_1_data_2;

  assign or_1_out = and_7_out | rom_1_data[7:0];  // OR_Gate or_1, 8 bits wide
  assign or_2_out = bit_extender_1_out | {register_2_q_2, register_2_q};  // OR_Gate or_2, 32 bits wide
  assign bit_extender_1_out = {{31{Reset_out}}, Reset_out};  // Bit_Extender bit_extender_1
  Button Reset (.out(Reset_out));
  Clock clock_1 (.out(clock_1_out));
  Register #(.trigger("falling")) Page (
    .D(or_3_out), .en(register_2_q_2[18]), .clk(or_4_out), .Q(Page_q), .clr(Reset_out));
  assign or_3_out = or_21_out | rom_1_data[23:16];  // OR_Gate or_3, 8 bits wide
  Multiplexer #(.width(8)) multiplexer_1 (
    .in0(rom_1_data[15:8]), .in1(PgCounter_q_2), .out(multiplexer_1_out), .sel(register_2_q_2[0]));
  ROM #(.addrWidth(16), .dataWidth(32)) rom_1 (.addr({PgCounter_q, PgCounter_q_2}), .data({rom_1_data_2, rom_1_data}));
  not not_1 (not_1_out, register_1_q);
  and and_1 (and_1_out, clock_1_out, not_1_out);
  buf or_4 (or_4_out, and_1_out);  // OR_Gate
  not not_2 (not_2_out, or_7_out);
  RAM #(.trigger("falling")) Ram256 (
    .addr(or_1_out), .we(or_2_out[6]), .oe(or_2_out[5]), .clk(or_4_out), .din(or_13_out), .dout(Ram256_dout));
  assign or_5_out = Page_q | rom_1_data[23:16];  // OR_Gate or_5, 8 bits wide
  or or_6 (or_6_out, or_9_out, Reset_out);
  Register #(.trigger("falling"), .width(16)) PgCounter (
    .D(multiplexer_2_out), .en(1'b1), .clk(or_4_out), .Q({PgCounter_q, PgCounter_q_2}), .clr(Reset_out));
  Multiplexer #(.width(16)) multiplexer_2 (
    .in0({PgCounter_q, adder_1_out}), .in1({or_5_out, or_8_out}), .out(multiplexer_2_out), .sel(or_6_out));
  or or_7 (or_7_out, xor_1_out[0], xor_1_out[1], xor_1_out[2], xor_1_out[3], xor_1_out[4], xor_1_out[5], xor_1_out[6], xor_1_out[7]);
  assign or_8_out = multiplexer_1_out | or_21_out;  // OR_Gate or_8, 8 bits wide
  Register #(.trigger("falling"), .width(1)) register_1 (
    .D(1'b1), .en(not_2_out), .clk(or_4_out), .Q(register_1_q), .clr(Reset_out));
  assign xor_1_out = rom_1_data_2 ^ 8'h5;  // XOR_Gate xor_1, 8 bits wide
  or or_9 (or_9_out, and_5_out, and_4_out, and_3_out, and_2_out, demultiplexer_1_out3, demultiplexer_1_out0);
  Adder adder_1 (.a(PgCounter_q_2), .b(8'h1), .out(adder_1_out));  // open: cin, cout
  and and_2 (and_2_out, or_22_out, demultiplexer_1_out1);
  ROM #(.dataWidth(32)) rom_2 (.addr(rom_1_data_2), .data(rom_2_data));
  RAM #(.trigger("falling")) Registers (
    .addr(or_1_out), .we(or_2_out[8]), .oe(or_2_out[7]), .clk(or_4_out), .din(or_13_out),
    .dout(Registers_dout));
  assign or_10_out = Ram256_dout | multiplexer_1_out;  // OR_Gate or_10, 8 bits wide
  and and_3 (and_3_out, demultiplexer_1_out2, or_22_out);
  and and_4 (and_4_out, demultiplexer_1_out4, or_22_out);
  and and_5 (and_5_out, demultiplexer_1_out5, or_22_out);
  Demultiplexer #(.select(5)) demultiplexer_1 (
    .out0(demultiplexer_1_out0), .out1(demultiplexer_1_out1), .out2(demultiplexer_1_out2),
    .out3(demultiplexer_1_out3), .out4(demultiplexer_1_out4), .out5(demultiplexer_1_out5), .in(and_6_out),
    .sel(rom_1_data_2[31:27]));  // open: out6, out7, out8, out9, out10, out11, out12, out13, out14, out15, out16, out17, out18, out19, out20, out21, out22, out23, out24, out25, out26, out27, out28, out29, out30, out31
  assign or_11_out = Registers_dout | or_10_out;  // OR_Gate or_11, 8 bits wide
  and and_6 (and_6_out, register_2_q_2[19], 1'b1);
  Register #(.trigger("low"), .width(32)) register_2 (
    .D(rom_2_data), .en(1'b1), .clk(or_4_out), .Q({register_2_q_2, register_2_q}), .clr(Reset_out));
  RAM #(.trigger("falling"), .\type ("nonvolatile")) Disc (
    .addr(or_1_out), .we(or_2_out[10]), .oe(or_2_out[9]), .clk(or_4_out), .din(or_13_out), .dout(Disc_dout));
  Button ClearDsp (.out(ClearDsp_out));
  // RGB_Video #(.cursor("No Cursor"), .height(32), .scale(8), .width(32)) rgb_video_1: pin names not known; wires that end beside it: rgb_video_1_p1, or_4_out, register_2_q[3], rgb_video_1_p4, rgb_video_1_p5, rgb_video_1_p6, rgb_video_1_p6
  or or_12 (rgb_video_1_p1, Reset_out, ClearDsp_out);
  assign or_13_out = multiplexer_1_out | or_39_out;  // OR_Gate or_13, 8 bits wide
  assign and_7_out = PtrReg_q & bit_extender_2_out;  // AND_Gate and_7, 8 bits wide
  assign or_14_out = or_11_out | Disc_dout;  // OR_Gate or_14, 8 bits wide
  Register #(.trigger("falling")) Color (
    .D(and_30_out), .en(register_2_q[2]), .clk(or_4_out),
    .Q({Color_q, rgb_video_1_p6[14:13], rgb_video_1_p6[9:8], rgb_video_1_p6[4:3]}), .clr(Reset_out));
  not not_3 (not_3_out, or_16_out);
  not not_4 (not_4_out, or_17_out);
  not not_5 (not_5_out, or_18_out);
  not not_6 (not_6_out, or_19_out);
  not not_7 (not_7_out, or_20_out);
  Register #(.trigger("falling"), .width(1)) Overflow (
    .D(or_15_out), .en(register_2_q_2[10]), .clk(or_4_out), .Q(Overflow_q), .clr(or_24_out));
  or or_15 (or_15_out, demultiplexer_2_out4, adder_2_cout);
  or or_16 (or_16_out, xor_2_out[0], xor_2_out[1], xor_2_out[2], xor_2_out[3], xor_2_out[4], xor_2_out[5], xor_2_out[6], xor_2_out[7]);
  or or_17 (or_17_out, xor_3_out[0], xor_3_out[1], xor_3_out[2], xor_3_out[3], xor_3_out[4], xor_3_out[5], xor_3_out[6], xor_3_out[7]);
  or or_18 (or_18_out, xor_4_out[0], xor_4_out[1], xor_4_out[2], xor_4_out[3], xor_4_out[4], xor_4_out[5], xor_4_out[6], xor_4_out[7]);
  or or_19 (or_19_out, xor_5_out[0], xor_5_out[1], xor_5_out[2], xor_5_out[3], xor_5_out[4], xor_5_out[5], xor_5_out[6], xor_5_out[7]);
  or or_20 (or_20_out, xor_6_out[0], xor_6_out[1], xor_6_out[2], xor_6_out[3], xor_6_out[4], xor_6_out[5], xor_6_out[6], xor_6_out[7]);
  Register #(.trigger("falling")) PtrReg (
    .D(AluOut_q), .en(register_2_q_2[16]), .clk(or_4_out), .Q(PtrReg_q), .clr(Reset_out));
  Register #(.trigger("falling"), .width(1)) Condition (
    .D(or_26_out), .en(or_25_out), .clk(or_4_out), .Q(Condition_q), .clr(or_23_out));
  Register #(.trigger("falling")) X (
    .D(and_30_out), .en(register_2_q[0]), .clk(or_4_out), .Q({X_q, rgb_video_1_p5}), .clr(Reset_out));
  assign xor_2_out = rom_1_data_2 ^ 8'he0;  // XOR_Gate xor_2, 8 bits wide
  assign xor_3_out = rom_1_data_2 ^ 8'he1;  // XOR_Gate xor_3, 8 bits wide
  assign xor_4_out = rom_1_data_2 ^ 8'he2;  // XOR_Gate xor_4, 8 bits wide
  assign xor_5_out = rom_1_data_2 ^ 8'he3;  // XOR_Gate xor_5, 8 bits wide
  assign xor_6_out = rom_1_data_2 ^ 8'he4;  // XOR_Gate xor_6, 8 bits wide
  assign or_21_out = or_14_out | and_11_out;  // OR_Gate or_21, 8 bits wide
  or or_22 (or_22_out, and_8_out, and_9_out);
  and and_8 (and_8_out, register_2_q_2[11], Overflow_q);
  and and_9 (and_9_out, Condition_q, register_2_q_2[13]);
  or or_23 (or_23_out, Reset_out, demultiplexer_2_out5);
  Register #(.trigger("falling")) Y (
    .D(and_30_out), .en(register_2_q[1]), .clk(or_4_out), .Q({Y_q, rgb_video_1_p4}), .clr(Reset_out));
  and and_10 (and_10_out, demultiplexer_2_out3, Overflow_q);
  or or_24 (or_24_out, demultiplexer_2_out7, Reset_out);
  or or_25 (or_25_out, demultiplexer_2_out6, register_2_q_2[12]);
  assign and_11_out = register_3_q & bit_extender_3_out;  // AND_Gate and_11, 8 bits wide
  or or_26 (or_26_out, and_10_out, or_38_out);
  Register #(.trigger("falling")) register_3 (
    .D(multiplexer_3_out), .en(or_27_out), .clk(or_4_out), .Q(register_3_q), .clr(Reset_out));
  Multiplexer #(.width(8)) multiplexer_3 (
    .in0(or_13_out), .in1(register_4_q), .out(multiplexer_3_out), .sel(not_3_out));
  or or_27 (or_27_out, not_7_out, not_6_out, not_3_out);
  or or_28 (or_28_out, not_5_out, not_4_out);
  assign bit_extender_2_out = {{7{register_2_q_2[17]}}, register_2_q_2[17]};  // Bit_Extender bit_extender_2
  Register #(.trigger("falling")) AluIeft (
    .D(or_21_out), .en(register_2_q_2[7]), .clk(or_4_out), .Q(AluIeft_q), .clr(Reset_out));
  Register #(.trigger("falling")) AluRight (
    .D(or_21_out), .en(register_2_q_2[8]), .clk(or_4_out), .Q(AluRight_q), .clr(Reset_out));
  Demultiplexer #(.select(5)) demultiplexer_2 (
    .out0(demultiplexer_2_out0), .out1(demultiplexer_2_out1), .out2(demultiplexer_2_out2),
    .out3(demultiplexer_2_out3), .out4(demultiplexer_2_out4), .out5(demultiplexer_2_out5),
    .out6(demultiplexer_2_out6), .out7(demultiplexer_2_out7), .in(and_12_out), .sel(rom_1_data_2[31:27]));  // open: out8, out9, out10, out11, out12, out13, out14, out15, out16, out17, out18, out19, out20, out21, out22, out23, out24, out25, out26, out27, out28, out29, out30, out31
  and and_12 (and_12_out, register_2_q_2[14], 1'b1);
  Register #(.trigger("falling")) register_4 (
    .D(multiplexer_4_out), .en(or_27_out), .clk(or_4_out), .Q(register_4_q), .clr(Reset_out));
  Multiplexer #(.width(8)) multiplexer_4 (
    .in0(register_3_q), .in1(register_5_q), .out(multiplexer_4_out), .sel(not_3_out));
  assign bit_extender_3_out = {{7{or_28_out}}, or_28_out};  // Bit_Extender bit_extender_3
  Demultiplexer #(.select(5)) demultiplexer_3 (
    .out0(demultiplexer_3_out0), .out1(demultiplexer_3_out1), .out2(demultiplexer_3_out2),
    .out3(demultiplexer_3_out3), .out4(demultiplexer_3_out4), .out5(demultiplexer_3_out5),
    .out6(demultiplexer_3_out6), .out7(demultiplexer_3_out7), .out8(demultiplexer_3_out8),
    .out9(demultiplexer_3_out9), .in(1'b1), .sel(rom_1_data_2[31:27]));  // open: out10, out11, out12, out13, out14, out15, out16, out17, out18, out19, out20, out21, out22, out23, out24, out25, out26, out27, out28, out29, out30, out31
  Register #(.trigger("falling")) register_5 (
    .D(multiplexer_5_out), .en(or_27_out), .clk(or_4_out), .Q(register_5_q), .clr(Reset_out));
  Multiplexer #(.width(8)) multiplexer_5 (
    .in0(register_4_q), .in1(register_6_q), .out(multiplexer_5_out), .sel(not_3_out));
  or or_29 (demultiplexer_3_out9, demultiplexer_3_out1, demultiplexer_3_out3);
  Register #(.trigger("falling")) register_6 (
    .D(multiplexer_6_out), .en(or_27_out), .clk(or_4_out), .Q(register_6_q), .clr(Reset_out));
  Multiplexer #(.width(8)) multiplexer_6 (
    .in0(register_5_q), .in1(register_7_q), .out(multiplexer_6_out), .sel(not_3_out));
  assign bit_extender_4_out = {{7{or_30_out}}, or_30_out};  // Bit_Extender bit_extender_4
  or or_30 (or_30_out, demultiplexer_3_out0, demultiplexer_3_out2);
  Adder adder_2 (.a(AluIeft_q), .b(and_21_out), .out(adder_2_out), .cin(demultiplexer_3_out2), .cout(adder_2_cout));
  assign bit_extender_5_out = {{7{demultiplexer_3_out9}}, demultiplexer_3_out9};  // Bit_Extender bit_extender_5
  Subtractor subtractor_1 (
    .a(AluIeft_q), .b(and_22_out), .out(subtractor_1_out), .bin(demultiplexer_3_out3));  // open: bout
  Comparator comparator_1 (
    .a(AluIeft_q), .b(AluRight_q), .gt(comparator_1_gt), .eq(comparator_1_eq), .lt(comparator_1_lt));
  assign bit_extender_6_out = {{7{demultiplexer_3_out8}}, demultiplexer_3_out8};  // Bit_Extender bit_extender_6
  Shifter shifter_1 (.in(AluIeft_q), .\dist (3'b001), .out(shifter_1_out));
  assign bit_extender_7_out = {{7{demultiplexer_3_out9}}, demultiplexer_3_out9};  // Bit_Extender bit_extender_7
  Shifter #(.shift("lr")) shifter_2 (.in(AluIeft_q), .\dist (3'b001), .out(shifter_2_out));
  assign bit_extender_8_out = {{7{demultiplexer_3_out6}}, demultiplexer_3_out6};  // Bit_Extender bit_extender_8
  assign and_13_out = AluIeft_q & AluRight_q;  // AND_Gate and_13, 8 bits wide
  assign bit_extender_9_out = {{7{demultiplexer_3_out7}}, demultiplexer_3_out7};  // Bit_Extender bit_extender_9
  assign or_31_out = AluIeft_q | AluRight_q;  // OR_Gate or_31, 8 bits wide
  assign and_14_out = bit_extender_4_out & adder_2_out;  // AND_Gate and_14, 8 bits wide
  assign or_32_out = and_14_out | and_15_out;  // OR_Gate or_32, 8 bits wide
  assign and_15_out = bit_extender_5_out & subtractor_1_out;  // AND_Gate and_15, 8 bits wide
  and and_16 (and_16_out, comparator_1_gt, demultiplexer_2_out2);
  assign and_17_out = bit_extender_6_out & shifter_1_out;  // AND_Gate and_17, 8 bits wide
  assign and_18_out = bit_extender_7_out & shifter_2_out;  // AND_Gate and_18, 8 bits wide
  assign and_19_out = bit_extender_8_out & and_13_out;  // AND_Gate and_19, 8 bits wide
  assign and_20_out = bit_extender_9_out & or_31_out;  // AND_Gate and_20, 8 bits wide
  Register #(.trigger("falling")) register_7 (
    .D(multiplexer_7_out), .en(or_27_out), .clk(or_4_out), .Q(register_7_q), .clr(Reset_out));
  Multiplexer #(.width(8)) multiplexer_7 (
    .in0(register_6_q), .in1(register_8_q), .out(multiplexer_7_out), .sel(not_3_out));
  not not_8 (not_8_out, demultiplexer_3_out2);
  not not_9 (not_9_out, demultiplexer_3_out3);
  assign and_21_out = bit_extender_12_out & AluRight_q;  // AND_Gate and_21, 8 bits wide
  assign and_22_out = bit_extender_11_out & AluRight_q;  // AND_Gate and_22, 8 bits wide
  and and_23 (and_23_out, comparator_1_eq, demultiplexer_2_out0);
  or or_33 (or_33_out, and_23_out, and_16_out);
  assign or_34_out = or_35_out | and_24_out | and_26_out;  // OR_Gate or_34, 8 bits wide
  assign or_35_out = and_17_out | and_18_out | and_19_out | and_20_out;  // OR_Gate or_35, 8 bits wide
  assign and_24_out = AluIeft_q & bit_extender_10_out;  // AND_Gate and_24, 8 bits wide
  assign bit_extender_10_out = {{7{demultiplexer_3_out4}}, demultiplexer_3_out4};  // Bit_Extender bit_extender_10
  Register #(.trigger("falling")) register_8 (
    .D(multiplexer_8_out), .en(or_27_out), .clk(or_4_out), .Q(register_8_q), .clr(Reset_out));
  Multiplexer #(.width(8)) multiplexer_8 (
    .in0(register_7_q), .in1(register_9_q), .out(multiplexer_8_out), .sel(not_3_out));
  assign bit_extender_11_out = {{7{not_8_out}}, not_8_out};  // Bit_Extender bit_extender_11
  assign bit_extender_12_out = {{7{not_9_out}}, not_9_out};  // Bit_Extender bit_extender_12
  and and_25 (and_25_out, comparator_1_lt, demultiplexer_2_out1);
  or or_36 (or_36_out, and_25_out, or_33_out);
  assign or_37_out = or_32_out | or_34_out;  // OR_Gate or_37, 8 bits wide
  or or_38 (or_38_out, and_28_out, or_36_out);
  assign and_26_out = AluRight_q & bit_extender_13_out;  // AND_Gate and_26, 8 bits wide
  assign bit_extender_13_out = {{7{demultiplexer_3_out5}}, demultiplexer_3_out5};  // Bit_Extender bit_extender_13
  Register #(.trigger("falling")) register_9 (
    .D(multiplexer_9_out), .en(or_27_out), .clk(or_4_out), .Q(register_9_q), .clr(Reset_out));
  Multiplexer #(.width(8)) multiplexer_9 (
    .in0(register_8_q), .in1(register_10_q), .out(multiplexer_9_out), .sel(not_3_out));
  Register #(.trigger("falling")) AluOut (
    .D(or_37_out), .en(register_2_q_2[9]), .clk(or_4_out), .Q(AluOut_q), .clr(Reset_out));
  and and_27 (and_27_out, AluOut_q[7], AluOut_q[6], AluOut_q[5], AluOut_q[4], AluOut_q[3], AluOut_q[2], AluOut_q[1], AluOut_q[0]);
  not not_10 (not_10_out, and_27_out);
  and and_28 (and_28_out, not_10_out, demultiplexer_2_out6);
  Register #(.trigger("falling")) register_10 (
    .D(multiplexer_10_out), .en(or_27_out), .clk(or_4_out), .Q(register_10_q), .clr(Reset_out));
  Multiplexer #(.width(8)) multiplexer_10 (
    .in0(register_9_q), .in1(register_11_q), .out(multiplexer_10_out), .sel(not_3_out));
  assign or_39_out = or_40_out | and_31_out;  // OR_Gate or_39, 8 bits wide
  assign or_40_out = and_29_out | and_30_out;  // OR_Gate or_40, 8 bits wide
  assign and_29_out = DataIn_q & bit_extender_14_out;  // AND_Gate and_29, 8 bits wide
  assign bit_extender_14_out = {{7{register_2_q_2[21]}}, register_2_q_2[21]};  // Bit_Extender bit_extender_14
  assign and_30_out = bit_extender_15_out & AluOut_q;  // AND_Gate and_30, 8 bits wide
  Register #(.trigger("falling")) register_11 (
    .D(multiplexer_11_out), .en(or_27_out), .clk(or_4_out), .Q(register_11_q), .clr(Reset_out));
  Multiplexer #(.width(8)) multiplexer_11 (
    .in0(register_10_q), .in1(register_12_q), .out(multiplexer_11_out), .sel(not_3_out));
  assign bit_extender_15_out = {{7{register_2_q_2[15]}}, register_2_q_2[15]};  // Bit_Extender bit_extender_15
  Register #(.trigger("falling")) register_12 (
    .D(multiplexer_12_out), .en(or_27_out), .clk(or_4_out), .Q(register_12_q), .clr(Reset_out));
  Multiplexer #(.width(8)) multiplexer_12 (
    .in0(register_11_q), .in1(register_13_q), .out(multiplexer_12_out), .sel(not_3_out));
  Register #(.trigger("falling")) DataIn (.Q(DataIn_q), .clr(Reset_out));  // open: D, en, clk
  Register #(.trigger("falling")) DataOut (
    .D(AluOut_q), .en(register_2_q_2[20]), .clk(or_4_out), .clr(Reset_out));  // open: Q
  Register #(.trigger("falling"), .width(1)) InFlag (.Q(InFlag_q[0]), .clr(or_44_out));  // open: D, en, clk
  Register #(.trigger("falling"), .width(1)) OutFlag (
    .D(1'b1), .en(not_12_out), .clk(or_4_out), .clr(Reset_out));  // open: Q
  Register #(.trigger("falling")) register_13 (
    .D(multiplexer_13_out), .en(or_27_out), .clk(or_4_out), .Q(register_13_q), .clr(Reset_out));
  Multiplexer #(.width(8)) multiplexer_13 (
    .in0(register_12_q), .in1(register_14_q), .out(multiplexer_13_out), .sel(not_3_out));
  not not_11 (not_11_out, or_41_out);
  or or_41 (or_41_out, xor_7_out[0], xor_7_out[1], xor_7_out[2], xor_7_out[3], xor_7_out[4], xor_7_out[5], xor_7_out[6], xor_7_out[7]);
  not not_12 (not_12_out, or_42_out);
  or or_42 (or_42_out, xor_8_out[0], xor_8_out[1], xor_8_out[2], xor_8_out[3], xor_8_out[4], xor_8_out[5], xor_8_out[6], xor_8_out[7]);
  not not_13 (not_13_out, or_43_out);
  or or_43 (or_43_out, xor_9_out[0], xor_9_out[1], xor_9_out[2], xor_9_out[3], xor_9_out[4], xor_9_out[5], xor_9_out[6], xor_9_out[7]);
  assign and_31_out = bit_extender_16_out & {{7{1'b0}}, InFlag_q[0]};  // AND_Gate and_31, 8 bits wide
  or or_44 (or_44_out, Reset_out, not_11_out);
  Register #(.trigger("falling")) register_14 (
    .D(multiplexer_14_out), .en(or_27_out), .clk(or_4_out), .Q(register_14_q), .clr(Reset_out));
  Multiplexer #(.width(8)) multiplexer_14 (
    .in0(register_13_q), .in1(register_15_q), .out(multiplexer_14_out), .sel(not_3_out));
  assign xor_7_out = rom_1_data_2 ^ 8'h10;  // XOR_Gate xor_7, 8 bits wide
  assign xor_8_out = rom_1_data_2 ^ 8'h11;  // XOR_Gate xor_8, 8 bits wide
  assign xor_9_out = rom_1_data_2 ^ 8'he;  // XOR_Gate xor_9, 8 bits wide
  assign bit_extender_16_out = {{7{not_13_out}}, not_13_out};  // Bit_Extender bit_extender_16
  Register #(.trigger("falling")) register_15 (
    .D(multiplexer_15_out), .en(or_27_out), .clk(or_4_out), .Q(register_15_q), .clr(Reset_out));
  Multiplexer #(.width(8)) multiplexer_15 (
    .in0(register_14_q), .in1(register_16_q), .out(multiplexer_15_out), .sel(not_3_out));
  Register #(.trigger("falling")) register_16 (
    .D(multiplexer_16_out), .en(or_27_out), .clk(or_4_out), .Q(register_16_q), .clr(Reset_out));
  Multiplexer #(.width(8)) multiplexer_16 (
    .in0(register_15_q), .in1(register_17_q), .out(multiplexer_16_out), .sel(not_3_out));
  Register #(.trigger("falling")) register_17 (
    .D(multiplexer_17_out), .en(or_27_out), .clk(or_4_out), .Q(register_17_q), .clr(Reset_out));
  Multiplexer #(.width(8)) multiplexer_17 (
    .in0(register_16_q), .in1(register_18_q), .out(multiplexer_17_out), .sel(not_3_out));
  Register #(.trigger("falling")) register_18 (
    .D(multiplexer_18_out), .en(or_27_out), .clk(or_4_out), .Q(register_18_q), .clr(Reset_out));
  Multiplexer #(.width(8)) multiplexer_18 (
    .in0(register_17_q), .in1(register_19_q), .out(multiplexer_18_out), .sel(not_3_out));
  Register #(.trigger("falling")) register_19 (
    .D(multiplexer_19_out), .en(or_27_out), .clk(or_4_out), .Q(register_19_q), .clr(Reset_out));
  Multiplexer #(.width(8)) multiplexer_19 (
    .in0(register_18_q), .in1(register_20_q), .out(multiplexer_19_out), .sel(not_3_out));
  Register #(.trigger("falling")) register_20 (
    .D(multiplexer_20_out), .en(or_27_out), .clk(or_4_out), .Q(register_20_q), .clr(Reset_out));
  Multiplexer #(.width(8)) multiplexer_20 (
    .in0(register_19_q), .in1(register_21_q), .out(multiplexer_20_out), .sel(not_3_out));
  Register #(.trigger("falling")) register_21 (
    .D(multiplexer_21_out), .en(or_27_out), .clk(or_4_out), .Q(register_21_q), .clr(Reset_out));
  Multiplexer #(.width(8)) multiplexer_21 (
    .in0(register_20_q), .in1(register_22_q), .out(multiplexer_21_out), .sel(not_3_out));
  Register #(.trigger("falling")) register_22 (
    .D(multiplexer_22_out), .en(or_27_out), .clk(or_4_out), .Q(register_22_q), .clr(Reset_out));
  Multiplexer #(.width(8)) multiplexer_22 (
    .in0(register_21_q), .in1(register_23_q), .out(multiplexer_22_out), .sel(not_3_out));
  Register #(.trigger("falling")) register_23 (
    .D(multiplexer_23_out), .en(or_27_out), .clk(or_4_out), .Q(register_23_q), .clr(Reset_out));
  Multiplexer #(.width(8)) multiplexer_23 (
    .in0(register_22_q), .in1(register_24_q), .out(multiplexer_23_out), .sel(not_3_out));
  Register #(.trigger("falling")) register_24 (
    .D(multiplexer_24_out), .en(or_27_out), .clk(or_4_out), .Q(register_24_q), .clr(Reset_out));
  Multiplexer #(.width(8)) multiplexer_24 (
    .in0(register_23_q), .in1(register_25_q), .out(multiplexer_24_out), .sel(not_3_out));
  Register #(.trigger("falling")) register_25 (
    .D(multiplexer_25_out), .en(or_27_out), .clk(or_4_out), .Q(register_25_q), .clr(Reset_out));
  Multiplexer #(.width(8)) multiplexer_25 (
    .in0(register_24_q), .in1({8{1'b0}}), .out(multiplexer_25_out), .sel(not_3_out));

  // Notes on the sheet:
  //   Address Bus
  //   contents of rom_1 (hex, n*v repeats v):
  //   0 1000000
  //   Program Memory
  //   DI Bus
  //   contents of rom_2 (hex, n*v repeats v):
  //   0 1 2 4 b 0 0 10 10 8
  //   Pop
  //   TopL
  //   TopR
  //   PshO
  //   PshCon
  //   Condition
  //   Overflow
  //   ALU Out to DI Bus Flag
  //   Clear Flg In
  //   Set Flg Out
  //   In Flg to DI
endmodule
